// Digital circuit 16-bit Zero.dig as structural Verilog
module _16_bit_Zero (
  input  [15:0] DIN,
  output ZR
);

  wire nor_1_out, nor_2_out, nor_3_out, not_1_out;

  nor nor_1 (nor_1_out, DIN[0], DIN[1], DIN[2], DIN[3], DIN[4]);
  nor nor_2 (nor_2_out, DIN[5], DIN[6], DIN[7], DIN[8], DIN[9]);
  nor nor_3 (nor_3_out, DIN[10], DIN[11], DIN[12], DIN[13], DIN[14]);
  not not_1 (not_1_out, DIN[15]);
  and and_1 (ZR, nor_1_out, nor_2_out, nor_3_out, not_1_out);
endmodule
