// Digital circuit ALU.dig as structural Verilog
module ALU (
  input  [15:0] A,
  input  [15:0] B,
  input  [5:0] ZA_NA_ZB_NB_F_NO,
  output [15:0] DOUT,
  output NG,
  output ZR
);

  wire nor_1_out, nor_2_out, nor_3_out, nor_4_out, not_1_out, not_2_out;
  wire [15:0] add_1_s, and_1_out, and_2_out, and_3_out, bitextender_1_out, bitextender_2_out,
       bitextender_3_out, bitextender_4_out, bitextender_5_out, multiplexer_1_out, xor_1_out, xor_2_out;

  not not_1 (not_1_out, ZA_NA_ZB_NB_F_NO[5]);
  not not_2 (not_2_out, ZA_NA_ZB_NB_F_NO[3]);
  BitExtender #(.inputBits(1)) bitextender_1 (.in(not_1_out), .out(bitextender_1_out));
  BitExtender #(.inputBits(1)) bitextender_2 (.in(not_2_out), .out(bitextender_2_out));
  assign and_1_out = bitextender_1_out & A;  // And and_1, 16 bits wide
  assign and_2_out = bitextender_2_out & B;  // And and_2, 16 bits wide
  BitExtender #(.inputBits(1)) bitextender_3 (.in(ZA_NA_ZB_NB_F_NO[4]), .out(bitextender_3_out));
  BitExtender #(.inputBits(1)) bitextender_4 (.in(ZA_NA_ZB_NB_F_NO[2]), .out(bitextender_4_out));
  assign xor_1_out = bitextender_3_out ^ and_1_out;  // XOr xor_1, 16 bits wide
  assign xor_2_out = bitextender_4_out ^ and_2_out;  // XOr xor_2, 16 bits wide
  assign and_3_out = xor_1_out & xor_2_out;  // And and_3, 16 bits wide
  Add #(.Bits(16)) add_1 (.a(xor_1_out), .b(xor_2_out), .c_i(1'b0), .s(add_1_s));  // open: c_o
  Multiplexer #(.Bits(16)) multiplexer_1 (
    .sel(ZA_NA_ZB_NB_F_NO[1]), .in_0(and_3_out), .in_1(add_1_s), .out(multiplexer_1_out));
  BitExtender #(.inputBits(1)) bitextender_5 (.in(ZA_NA_ZB_NB_F_NO[0]), .out(bitextender_5_out));
  assign DOUT = bitextender_5_out ^ multiplexer_1_out;  // XOr xor_3, 16 bits wide
  nor nor_1 (nor_1_out, DOUT[0], DOUT[1]);
  nor nor_2 (nor_2_out, DOUT[2], DOUT[3], DOUT[4], DOUT[5]);
  nor nor_3 (nor_3_out, DOUT[6], DOUT[7], DOUT[8], DOUT[9], DOUT[10]);
  nor nor_4 (nor_4_out, DOUT[11], DOUT[12], DOUT[13], DOUT[14], DOUT[15]);
  and and_4 (ZR, nor_1_out, nor_2_out, nor_3_out, nor_4_out);

  assign NG = DOUT[15];
endmodule
