// Digital circuit CPU.dig as structural Verilog
module CPU (
  input  [15:0] DIN,
  input  [15:0] INS,
  input  CLK,
  input  CLR,
  output [15:0] DOUT,
  output WRT,
  output [14:0] ADDR,
  output [14:0] PC
);

  wire alu_1_ng, alu_1_zr, jump_decode_1_jmp, not_1_out, not_2_out, or_1_out, store_decode_1_a,
       store_decode_1_d;
  wire [15:0] D_q, multiplexer_1_out, multiplexer_2_out;
  wire [15:15] A_q;

  Multiplexer #(.Bits(16)) multiplexer_1 (.sel(INS[15]), .in_0(INS), .in_1(DOUT), .out(multiplexer_1_out));
  not not_1 (not_1_out, INS[15]);
  Store_Decode store_decode_1 (.DIN(INS[5:3]), .C(INS[15]), .A(store_decode_1_a), .D(store_decode_1_d), .M(WRT));
  Register #(.Bits(16)) D (.D(DOUT), .C(CLK), .en(store_decode_1_d), .Q(D_q));
  or or_1 (or_1_out, not_1_out, store_decode_1_a);
  Register #(.Bits(16)) A (.D(multiplexer_1_out), .C(CLK), .en(or_1_out), .Q({A_q[15], ADDR}));
  ALU alu_1 (.A(D_q), .B(multiplexer_2_out), .ZA_NA_ZB_NB_F_NO(INS[11:6]), .DOUT(DOUT), .NG(alu_1_ng), .ZR(alu_1_zr));
  Multiplexer #(.Bits(16)) multiplexer_2 (.sel(INS[12]), .in_0({A_q[15], ADDR}), .in_1(DIN), .out(multiplexer_2_out));
  Jump_Decode jump_decode_1 (.DIN(INS[2:0]), .ZR(alu_1_zr), .C(INS[15]), .NG(alu_1_ng), .JMP(jump_decode_1_jmp));
  not not_2 (not_2_out, jump_decode_1_jmp);
  CounterPreset #(.Bits(15)) counterpreset_1 (
    .en(not_2_out), .C(CLK), .dir(1'b0), .in(ADDR), .ld(jump_decode_1_jmp), .clr(CLR), .out(PC));  // open: ovf
endmodule
