// Digital circuit GPU.dig as structural Verilog
module GPU (
  input  [15:0] DIN,
  input  CLK,
  input  CLR,
  output [31:0] DOUT,
  output [5:0] ADDR,
  output [4:0] ROW
);

  wire decoder_1_out_0, decoder_1_out_1, decoder_1_out_2, or_1_out, or_2_out;
  wire [1:0] counter_1_out;

  or or_1 (or_1_out, CLR, decoder_1_out_2);
  Register #(.Bits(16)) register_1 (.D(DIN), .C(CLK), .en(decoder_1_out_0), .Q(DOUT[15:0]));
  Register #(.Bits(16)) register_2 (.D(DIN), .C(CLK), .en(decoder_1_out_2), .Q(DOUT[31:16]));
  Counter #(.Bits(2)) counter_1 (.en(CLK), .C(CLK), .clr(or_1_out), .out(counter_1_out));  // open: ovf
  Decoder #(.Selector_Bits(2)) decoder_1 (
    .sel(counter_1_out), .out_0(decoder_1_out_0), .out_1(decoder_1_out_1), .out_2(decoder_1_out_2));  // open: out_3
  or or_2 (or_2_out, decoder_1_out_0, decoder_1_out_2);
  Counter #(.Bits(6)) counter_2 (.en(or_2_out), .C(CLK), .clr(CLR), .out(ADDR));  // open: ovf
  Counter #(.Bits(5)) counter_3 (.en(decoder_1_out_1), .C(CLK), .clr(CLR), .out(ROW));  // open: ovf
endmodule
