// Digital circuit Jump Decode.dig as structural Verilog
module Jump_Decode (
  input  [2:0] DIN,
  input  ZR,
  input  C,
  input  NG,
  output JMP
);

  wire and_1_out, and_2_out, and_3_out, and_4_out, and_5_out, and_6_out, decoder_1_out_1, decoder_1_out_2,
       decoder_1_out_3, decoder_1_out_4, decoder_1_out_5, decoder_1_out_6, decoder_1_out_7, nor_1_out,
       not_1_out, not_2_out, or_1_out, or_2_out, or_3_out, or_4_out;

  Decoder #(.Selector_Bits(3)) decoder_1 (
    .sel(DIN), .out_1(decoder_1_out_1), .out_2(decoder_1_out_2), .out_3(decoder_1_out_3),
    .out_4(decoder_1_out_4), .out_5(decoder_1_out_5), .out_6(decoder_1_out_6), .out_7(decoder_1_out_7));  // open: out_0
  nor nor_1 (nor_1_out, NG, ZR);
  or or_1 (or_1_out, NG, ZR);
  not not_1 (not_1_out, NG);
  not not_2 (not_2_out, ZR);
  and and_1 (and_1_out, nor_1_out, decoder_1_out_1);
  and and_2 (and_2_out, ZR, decoder_1_out_2);
  and and_3 (and_3_out, not_1_out, decoder_1_out_3);
  and and_4 (and_4_out, NG, decoder_1_out_4);
  and and_5 (and_5_out, not_2_out, decoder_1_out_5);
  and and_6 (and_6_out, or_1_out, decoder_1_out_6);
  or or_2 (or_2_out, and_1_out, and_2_out, and_3_out, and_4_out, and_5_out);
  or or_3 (or_3_out, and_6_out, decoder_1_out_7);
  or or_4 (or_4_out, or_2_out, or_3_out);
  and and_7 (JMP, C, or_4_out);
endmodule
