// Digital circuit Keyboard Decode.dig as structural Verilog
module Keyboard_Decode (
  input  [14:0] ADDR,
  input  [15:0] DIN,
  output WRT
);

  wire _16_bit_zero_1_zr, and_1_out, and_2_out, and_3_out, and_4_out, and_5_out, not_1_out;

  _16_bit_Zero _16_bit_zero_1 (.DIN(DIN), .ZR(_16_bit_zero_1_zr));
  and and_1 (and_1_out, ADDR[0], ADDR[1], ADDR[2], ADDR[3], ADDR[4]);
  and and_2 (and_2_out, ADDR[5], ADDR[7], ADDR[8], ADDR[9], ADDR[10]);
  and and_3 (and_3_out, ADDR[11], ADDR[12], ADDR[13], ADDR[14]);
  and and_4 (and_4_out, and_1_out, and_2_out, and_3_out);
  not not_1 (not_1_out, ADDR[6]);
  and and_5 (and_5_out, not_1_out, and_4_out);
  and and_6 (WRT, and_5_out, _16_bit_zero_1_zr);
endmodule
