// Digital circuit Store Decode.dig as structural Verilog
module Store_Decode (
  input  [2:0] DIN,
  input  C,
  output A,
  output D,
  output M
);

  and and_1 (M, C, DIN[0]);
  and and_2 (D, C, DIN[1]);
  and and_3 (A, C, DIN[2]);
endmodule
