// Logisim project hack.circ as structural Verilog: 13 circuits, main circuit CPU
module ALU (
  input  [5:0] ZA_NA_ZB_NB_F_NO,
  input  [15:0] A,
  input  [15:0] B,
  output [15:0] OUT,
  output NG,
  output ZR
);

  wire not_1_out, not_2_out;
  wire [15:0] adder_1_out, and_1_out, and_2_out, and_3_out, bit_extender_1_out, bit_extender_2_out,
       bit_extender_3_out, bit_extender_4_out, bit_extender_5_out, multiplexer_1_out, xor_1_out, xor_2_out;

  assign bit_extender_1_out = {{15{ZA_NA_ZB_NB_F_NO[2]}}, ZA_NA_ZB_NB_F_NO[2]};  // Bit_Extender bit_extender_1
  assign bit_extender_2_out = {{15{ZA_NA_ZB_NB_F_NO[4]}}, ZA_NA_ZB_NB_F_NO[4]};  // Bit_Extender bit_extender_2
  assign bit_extender_3_out = {{15{not_2_out}}, not_2_out};  // Bit_Extender bit_extender_3
  assign bit_extender_4_out = {{15{not_1_out}}, not_1_out};  // Bit_Extender bit_extender_4
  not not_1 (not_1_out, ZA_NA_ZB_NB_F_NO[3]);
  not not_2 (not_2_out, ZA_NA_ZB_NB_F_NO[5]);
  assign and_1_out = A & bit_extender_3_out;  // AND_Gate and_1, 16 bits wide
  assign and_2_out = B & bit_extender_4_out;  // AND_Gate and_2, 16 bits wide
  assign xor_1_out = bit_extender_2_out ^ and_1_out;  // XOR_Gate xor_1, 16 bits wide
  assign xor_2_out = bit_extender_1_out ^ and_2_out;  // XOR_Gate xor_2, 16 bits wide
  assign and_3_out = xor_1_out & xor_2_out;  // AND_Gate and_3, 16 bits wide
  Adder #(.width(16)) adder_1 (.a(xor_1_out), .b(xor_2_out), .out(adder_1_out));  // open: cin, cout
  Multiplexer #(.width(16), .enable("false")) multiplexer_1 (
    .in0(and_3_out), .in1(adder_1_out), .out(multiplexer_1_out), .sel(ZA_NA_ZB_NB_F_NO[1]));
  assign bit_extender_5_out = {{15{ZA_NA_ZB_NB_F_NO[0]}}, ZA_NA_ZB_NB_F_NO[0]};  // Bit_Extender bit_extender_5
  assign {NG, OUT[14:0]} = bit_extender_5_out ^ multiplexer_1_out;  // XOR_Gate xor_3, 16 bits wide
  nor nor_1 (ZR, NG, OUT[14], OUT[13], OUT[12], OUT[11], OUT[10], OUT[9], OUT[8], OUT[7], OUT[6], OUT[5], OUT[4], OUT[3], OUT[2], OUT[1], OUT[0]);

  assign OUT[15] = NG;
endmodule

module CPU (
  input  [15:0] INS,
  input  [15:0] DIN,
  input  CLK,
  input  RST,
  output [15:0] DOUT,
  output WRT,
  output [14:0] ADDR,
  output [14:0] PC
);

  wire alu_1_ng, alu_1_zr, jump_decoder_1_jmp, not_1_out, not_2_out, or_1_out, store_decoder_1_a,
       store_decoder_1_d;
  wire [15:0] D_q, multiplexer_1_out, multiplexer_2_out;
  wire [15:15] A_q;

  STORE_DECODER store_decoder_1 (.DIN(INS[5:3]), .A(store_decoder_1_a), .D(store_decoder_1_d), .M(WRT), .C(INS[15]));
  Multiplexer #(.width(16), .enable("false")) multiplexer_1 (
    .in0(INS), .in1(DOUT), .out(multiplexer_1_out), .sel(INS[15]));
  not not_1 (not_1_out, INS[15]);
  or or_1 (or_1_out, store_decoder_1_a, not_1_out);
  Register #(.width(16)) A (.D(multiplexer_1_out), .en(or_1_out), .Q({A_q[15], ADDR}), .clk(CLK), .clr(RST));
  Register #(.width(16)) D (.D(DOUT), .en(store_decoder_1_d), .Q(D_q), .clk(CLK), .clr(RST));
  Multiplexer #(.width(16), .enable("false")) multiplexer_2 (
    .in0({A_q[15], ADDR}), .in1(DIN), .out(multiplexer_2_out), .sel(INS[12]));
  ALU alu_1 (.A(D_q), .B(multiplexer_2_out), .OUT(DOUT), .ZA_NA_ZB_NB_F_NO(INS[11:6]), .NG(alu_1_ng), .ZR(alu_1_zr));
  not not_2 (not_2_out, jump_decoder_1_jmp);
  JUMP_DECODER jump_decoder_1 (.DIN(INS[2:0]), .JMP(jump_decoder_1_jmp), .NG(alu_1_ng), .ZR(alu_1_zr), .C(INS[15]));
  Counter #(.width(15), .max('h7fff)) counter_1 (
    .load(jump_decoder_1_jmp), .D(ADDR), .count(not_2_out), .Q(PC), .clk(CLK), .clr(RST));  // open: carry
endmodule

module JUMP_DECODER (
  input  NG,
  input  C,
  input  ZR,
  input  [2:0] DIN,
  output JMP
);

  wire and_1_out, and_2_out, and_3_out, and_4_out, and_5_out, and_6_out, decoder_1_out1, decoder_1_out2,
       decoder_1_out3, decoder_1_out4, decoder_1_out5, decoder_1_out6, decoder_1_out7, nor_1_out, not_1_out,
       not_2_out, or_1_out, or_2_out;

  Decoder #(.select(3), .enable("false")) decoder_1 (
    .out1(decoder_1_out1), .out2(decoder_1_out2), .out3(decoder_1_out3), .out4(decoder_1_out4),
    .out5(decoder_1_out5), .out6(decoder_1_out6), .out7(decoder_1_out7), .sel(DIN));  // open: out0
  not not_1 (not_1_out, ZR);
  nor nor_1 (nor_1_out, ZR, NG);
  not not_2 (not_2_out, NG);
  or or_1 (or_1_out, ZR, NG);
  and and_1 (and_1_out, nor_1_out, decoder_1_out1);
  and and_2 (and_2_out, ZR, decoder_1_out2);
  and and_3 (and_3_out, not_2_out, decoder_1_out3);
  and and_4 (and_4_out, NG, decoder_1_out4);
  and and_5 (and_5_out, not_1_out, decoder_1_out5);
  and and_6 (and_6_out, or_1_out, decoder_1_out6);
  or or_2 (or_2_out, and_1_out, and_2_out, and_3_out, and_4_out, and_5_out, and_6_out, decoder_1_out7);
  and and_7 (JMP, C, or_2_out);
endmodule

module COMPUTER (
);

  wire and_1_out, clock_1_out, cpu_1_wrt, gpu_address_decode_1_wrt_2, keyboard_1_avail,
       keyboard_address_decoder_1_out, or_1_out, RESET_out;
  wire [5:0] gpu_address_decode_1_addr_2;
  wire [6:0] keyboard_1_data;
  wire [14:0] cpu_1_addr, cpu_1_pc;
  wire [15:0] bit_extender_1_out, cpu_1_dout, multiplexer_1_out, ram_1_data, rom_1_data;
  wire [31:0] n32x32_gpu_1_row_0, n32x32_gpu_1_row_1, n32x32_gpu_1_row_2, n32x32_gpu_1_row_3,
       n32x32_gpu_1_row_4, n32x32_gpu_1_row_5, n32x32_gpu_1_row_6, n32x32_gpu_1_row_7, n32x32_gpu_1_row_8,
       n32x32_gpu_1_row_9, n32x32_gpu_1_row_10, n32x32_gpu_1_row_11, n32x32_gpu_1_row_12,
       n32x32_gpu_1_row_13, n32x32_gpu_1_row_14, n32x32_gpu_1_row_15, n32x32_gpu_1_row_16,
       n32x32_gpu_1_row_17, n32x32_gpu_1_row_18, n32x32_gpu_1_row_19, n32x32_gpu_1_row_20,
       n32x32_gpu_1_row_21, n32x32_gpu_1_row_22, n32x32_gpu_1_row_23, n32x32_gpu_1_row_24,
       n32x32_gpu_1_row_25, n32x32_gpu_1_row_26, n32x32_gpu_1_row_27, n32x32_gpu_1_row_28,
       n32x32_gpu_1_row_29, n32x32_gpu_1_row_30, n32x32_gpu_1_row_31;

  Clock clock_1 (.out(clock_1_out));
  Multiplexer #(.width(16), .enable("false")) multiplexer_1 (
    .in0(cpu_1_dout), .in1(bit_extender_1_out), .out(multiplexer_1_out), .sel(keyboard_address_decoder_1_out));
  or or_1 (or_1_out, and_1_out, cpu_1_wrt);
  and and_1 (and_1_out, keyboard_1_avail, keyboard_address_decoder_1_out);
  ROM #(.addrWidth(15), .dataWidth(16)) rom_1 (.addr(cpu_1_pc), .data(rom_1_data), .sel(1'b1));
  RAM #(.addrWidth(15), .dataWidth(16), .bus("separate")) ram_1 (
    .addr(cpu_1_addr), .din(multiplexer_1_out), .data(ram_1_data), .str(or_1_out), .sel(1'b1),
    .clk(clock_1_out), .ld(1'b1), .clr(RESET_out));
  KEYBOARD_ADDRESS_DECODER keyboard_address_decoder_1 (.ADDR(cpu_1_addr), .OUT(keyboard_address_decoder_1_out));
  Keyboard keyboard_1 (
    .clk(clock_1_out), .re(keyboard_address_decoder_1_out), .clr(RESET_out), .avail(keyboard_1_avail),
    .data(keyboard_1_data));
  Button RESET (.out(RESET_out));
  CPU cpu_1 (
    .INS(rom_1_data), .DIN(ram_1_data), .CLK(clock_1_out), .DOUT(cpu_1_dout), .WRT(cpu_1_wrt),
    .ADDR(cpu_1_addr), .PC(cpu_1_pc), .RST(RESET_out));
  assign bit_extender_1_out = {{9{1'b0}}, keyboard_1_data};  // Bit_Extender bit_extender_1
  GPU_ADDRESS_DECODE gpu_address_decode_1 (
    .ADDR(cpu_1_addr), .WRT(cpu_1_wrt), .ADDR_2(gpu_address_decode_1_addr_2),
    .WRT_2(gpu_address_decode_1_wrt_2));
  DotMatrix #(.matrixcols(32), .matrixrows(32)) dotmatrix_1 (
    .col0(n32x32_gpu_1_row_0), .col1(n32x32_gpu_1_row_1), .col2(n32x32_gpu_1_row_2),
    .col3(n32x32_gpu_1_row_3), .col4(n32x32_gpu_1_row_4), .col5(n32x32_gpu_1_row_5),
    .col6(n32x32_gpu_1_row_6), .col7(n32x32_gpu_1_row_7), .col8(n32x32_gpu_1_row_8),
    .col9(n32x32_gpu_1_row_9), .col10(n32x32_gpu_1_row_10), .col11(n32x32_gpu_1_row_11),
    .col12(n32x32_gpu_1_row_12), .col13(n32x32_gpu_1_row_13), .col14(n32x32_gpu_1_row_14),
    .col15(n32x32_gpu_1_row_15), .col16(n32x32_gpu_1_row_16), .col17(n32x32_gpu_1_row_17),
    .col18(n32x32_gpu_1_row_18), .col19(n32x32_gpu_1_row_19), .col20(n32x32_gpu_1_row_20),
    .col21(n32x32_gpu_1_row_21), .col22(n32x32_gpu_1_row_22), .col23(n32x32_gpu_1_row_23),
    .col24(n32x32_gpu_1_row_24), .col25(n32x32_gpu_1_row_25), .col26(n32x32_gpu_1_row_26),
    .col27(n32x32_gpu_1_row_27), .col28(n32x32_gpu_1_row_28), .col29(n32x32_gpu_1_row_29),
    .col30(n32x32_gpu_1_row_30), .col31(n32x32_gpu_1_row_31));
  _32x32_GPU u_32x32_gpu_1 (
    .DIN(cpu_1_dout), .ADDR(gpu_address_decode_1_addr_2), .WRT(gpu_address_decode_1_wrt_2),
    .CLK(clock_1_out), .ROW_0(n32x32_gpu_1_row_0), .ROW_1(n32x32_gpu_1_row_1), .ROW_2(n32x32_gpu_1_row_2),
    .ROW_3(n32x32_gpu_1_row_3), .ROW_4(n32x32_gpu_1_row_4), .ROW_5(n32x32_gpu_1_row_5),
    .ROW_6(n32x32_gpu_1_row_6), .ROW_7(n32x32_gpu_1_row_7), .ROW_8(n32x32_gpu_1_row_8),
    .ROW_9(n32x32_gpu_1_row_9), .ROW_10(n32x32_gpu_1_row_10), .ROW_11(n32x32_gpu_1_row_11),
    .ROW_12(n32x32_gpu_1_row_12), .ROW_13(n32x32_gpu_1_row_13), .ROW_14(n32x32_gpu_1_row_14),
    .ROW_15(n32x32_gpu_1_row_15), .ROW_16(n32x32_gpu_1_row_16), .ROW_17(n32x32_gpu_1_row_17),
    .ROW_18(n32x32_gpu_1_row_18), .ROW_19(n32x32_gpu_1_row_19), .ROW_20(n32x32_gpu_1_row_20),
    .ROW_21(n32x32_gpu_1_row_21), .ROW_22(n32x32_gpu_1_row_22), .ROW_23(n32x32_gpu_1_row_23),
    .ROW_24(n32x32_gpu_1_row_24), .ROW_25(n32x32_gpu_1_row_25), .ROW_26(n32x32_gpu_1_row_26),
    .ROW_27(n32x32_gpu_1_row_27), .ROW_28(n32x32_gpu_1_row_28), .ROW_29(n32x32_gpu_1_row_29),
    .ROW_30(n32x32_gpu_1_row_30), .ROW_31(n32x32_gpu_1_row_31), .CLR(RESET_out));

  // Notes on the sheet:
  //   contents of rom_1 (hex, n*v repeats v):
  //   100 ec10 0 e308 400 ec10 1 e308 800 ec10 2 e308 1000 ec10 3 e308 2000 ec10 4 e308 40 ec10 0 fde8
  //   eca0 e308 1 fc10 0 fde8 eca0 e308 2 fc10 0 fde8 eca0 e308 3 fc10 0 fde8 eca0 e308 4 fc10 0 fde8 eca0
  //   e308 5 ec10 0 e090 0 f1d0 2 e308 0 fc10 1 e308 2435 ea87 252c ea87 100 ec10 0 e308 400 ec10 1 e308
  //   800 ec10 2 e308 1000 ec10 3 e308 2000 ec10 4 e308 0 ec10 61 e302 0 fde8 eca0 ea88 e390 58 ea87 7fc0
  //   ec10 0 fde8 eca0 e308 0 fca8 fc10 80 e308 40 ec10 0 fde8 eca0 e308 0 fca8 fc10 81 e308 0 ec10 0 fde8
  //   eca0 e308 5 ec10 1 f1e0 fc10 d e308 0 fca0 fc10 2 fc20 e308 edd0 0 e308 1 fca0 fc10 4 e308 2 ec10 1
  //   f1e0 fc10 3 e308 3 ec10 1 f1e0 fc10 2 e308 4 ec10 1 f1e0 fc10 1 e308 d fc20 ea87 3 ec10 b5 e302 0
  //   fde8 eca0 ea88 e390 ac ea87 0 ec10 2 f0a0 fc10 0 fde8 eca0 e308 0 ec10 2 f0a0 fc10 0 fde8 eca0 e308
  //   80 fc10 0 fde8 eca0 e308 0 fca8 fc10 eca0 f088 0 fca8 fc10 eca0 f088 1 ec10 1 f090 d e308 0 fca8
  //   fc10 d fc20 e308 f ec10 0 fde8 eca0 e308 1 ec10 2 f0a0 fc10 0 fde8 eca0 e308 0 fca8 fc10 eca0 f4d0
  //   fe e301 0 fca0 ea88 101 ea87 0 fca0 efc8 0 fca0 fc10 109 e302 ea90 10a ea87 efd0 0 fca0 e308 0 fca0
  //   fc10 154 e301 10 ec10 0 fde8 eca0 e308 1 ec10 2 f0a0 fc10 0 fde8 eca0 e308 0 fca8 fc10 eca0 f4c8 1
  //   ec10 2 f090 d e308 0 fca8 fc10 d fc20 e308 1 ec10 0 fde8 eca0 e308 1 ec10 1 f0a0 fc10 0 fde8 eca0
  //   e308 0 fca8 fc10 eca0 f088 1 ec10 1 f090 d e308 0 fca8 fc10 d fc20 e308 154 ea87 1 ec10 1 f0a0 fc10
  //   0 fde8 eca0 e308 189 ec10 0 fde8 eca0 e308 1 fc10 0 fde8 eca0 e308 2 fc10 0 fde8 eca0 e308 3 fc10 0
  //   fde8 eca0 e308 4 fc10 0 fde8 eca0 e308 5 ec10 1 e090 0 f1d0 2 e308 0 fc10 1 e308 1e9d ea87 0 ec10 1
  //   f090 d e308 0 fca8 fc10 d fc20 e308 1 ec10 2 f0a0 fc10 0 fde8 eca0 e308 f ec10 0 fde8 eca0 e308 0
  //   fca8 fc10 eca0 f4c8 1d5 ec10 0 fde8 eca0 e308 1 fc10 0 fde8 eca0 e308 2 fc10 0 fde8 eca0 e308 3 fc10
  //   0 fde8 eca0 e308 4 fc10 0 fde8 eca0 e308 5 ec10 1 e090 0 f1d0 2 e308 0 fc10 1 e308 fad ea87 2 ec10 1
  //   f090 d e308 0 fca8 fc10 d fc20 e308 1 ec10 1 f0a0 fc10 0 fde8 eca0 e308 0 ec10 1 f0a0 fc10 0 fde8
  //   eca0 e308 2 ec10 1 f0a0 fc10 0 fde8 eca0 e308 0 fca8 fc10 eca0 f548 22d ec10 0 fde8 eca0 e308 1 fc10
  //   0 fde8 eca0 e308 2 fc10 0 fde8 eca0 e308 3 fc10 0 fde8 eca0 e308 4 fc10 0 fde8 eca0 e308 5 ec10 2
  //   e090 0 f1d0 2 e308 0 fc10 1 e308 1ef7 ea87 0 fca8 fc10 82 e308 0 ec10 1 f0a0 fc10 0 fde8 eca0 e308 5
  //   ec10 1 f1e0 fc10 d e308 0 fca0 fc10 2 fc20 e308 edd0 0 e308 1 fca0 fc10 4 e308 2 ec10 1 f1e0 fc10 3
  //   e308 3 ec10 1 f1e0 fc10 2 e308 4 ec10 1 f1e0 fc10 1 e308 d fc20 ea87 a ec10 273 e302 0 fde8 eca0
  //   ea88 e390 26a ea87 3 ec10 2 f0a0 fc10 0 fde8 eca0 e308 1 ec10 2 f0a0 fc10 0 fde8 eca0 e308 0 fca8
  //   fc10 eca0 f4d0 291 e302 0 fca0 ea88 294 ea87 0 fca0 efc8 0 fca0 fc10 29c e302 ea90 29d ea87 efd0 0
  //   fca0 e308 0 fca0 fc10 371 e301 2 ec10 2 f0a0 fc10 0 fde8 eca0 e308 0 ec10 2 f0a0 fc10 0 fde8 eca0
  //   e308 0 fca8 fc10 eca0 f4d0 2c3 e304 0 fca0 ea88 2c6 ea87 0 fca0 efc8 0 fca0 fc10 2ce e302 ea90 2cf
  //   ea87 efd0 0 fca0 e308 0 fca0 fc10 33c e301 0 ec10 2 f0a0 fc10 0 fde8 eca0 e308 2 ec10 2 f0a0 fc10 0
  //   fde8 eca0 e308 315 ec10 0 fde8 eca0 e308 1 fc10 0 fde8 eca0 e308 2 fc10 0 fde8 eca0 e308 3 fc10 0
  //   fde8 eca0 e308 4 fc10 0 fde8 eca0 e308 5 ec10 2 e090 0 f1d0 2 e308 0 fc10 1 e308 aa ea87 0 fca8 fc10
  //   82 e308 1 ec10 0 fde8 eca0 e308 0 ec10 2 f0a0 fc10 0 fde8 eca0 e308 0 fca8 fc10 eca0 f088 0 ec10 2
  //   f090 d e308 0 fca8 fc10 d fc20 e308 2a5 ea87 0 ec10 0 fde8 eca0 e308 5 ec10 1 f1e0 fc10 d e308 0
  //   fca0 fc10 2 fc20 e308 edd0 0 e308 1 fca0 fc10 4 e308 2 ec10 1 f1e0 fc10 3 e308 3 ec10 1 f1e0 fc10 2
  //   e308 4 ec10 1 f1e0 fc10 1 e308 d fc20 ea87 5ff ea87 2 ec10 2 f0a0 fc10 0 fde8 eca0 e308 0 ec10 2
  //   f0a0 fc10 0 fde8 eca0 e308 0 fca8 fc10 eca0 f4c8 3b4 ec10 0 fde8 eca0 e308 1 fc10 0 fde8 eca0 e308 2
  //   fc10 0 fde8 eca0 e308 3 fc10 0 fde8 eca0 e308 4 fc10 0 fde8 eca0 e308 5 ec10 1 e090 0 f1d0 2 e308 0
  //   fc10 1 e308 14d2 ea87 0 ec10 1 f090 d e308 0 fca8 fc10 d fc20 e308 3 ec10 2 f0a0 fc10 0 fde8 eca0
  //   e308 1 ec10 2 f0a0 fc10 0 fde8 eca0 e308 0 fca8 fc10 eca0 f4c8 403 ec10 0 fde8 eca0 e308 1 fc10 0
  //   fde8 eca0 e308 2 fc10 0 fde8 eca0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
endmodule

module STORE_DECODER (
  input  C,
  input  [2:0] DIN,
  output A,
  output D,
  output M
);

  and and_1 (A, C, DIN[2]);
  and and_2 (D, C, DIN[1]);
  and and_3 (M, C, DIN[0]);
endmodule

module GPU_ADDRESS_DECODE (
  input  [14:0] ADDR,
  input  WRT,
  output [5:0] ADDR_2,
  output WRT_2
);

  wire and_1_out;
  wire [5:0] bit_extender_1_out;

  and and_1 (and_1_out, ADDR[6], ADDR[7], ADDR[8], ADDR[9], ADDR[10], ADDR[11], ADDR[12], ADDR[13], ADDR[14]);
  assign bit_extender_1_out = {{5{and_1_out}}, and_1_out};  // Bit_Extender bit_extender_1
  assign ADDR_2 = ADDR[5:0] & bit_extender_1_out;  // AND_Gate and_2, 6 bits wide
  and and_3 (WRT_2, and_1_out, WRT);
endmodule

module _2_ROW_GPU (
  input  [15:0] DIN,
  input  ADDR,
  input  WRT,
  input  CLK,
  input  CLR,
  output [15:0] ROW_0,
  output [15:0] ROW_1
);

  wire demultiplexer_1_out0, demultiplexer_1_out1;

  Demultiplexer #(.enable("false")) demultiplexer_1 (
    .out0(demultiplexer_1_out0), .out1(demultiplexer_1_out1), .in(WRT), .sel(ADDR));
  Register #(.width(16)) register_1 (.D(DIN), .en(demultiplexer_1_out0), .Q(ROW_0), .clk(CLK), .clr(CLR));
  Register #(.width(16)) register_2 (.D(DIN), .en(demultiplexer_1_out1), .Q(ROW_1), .clk(CLK), .clr(CLR));
endmodule

module _4_ROW_GPU (
  input  [15:0] DIN,
  input  [1:0] ADDR,
  input  WRT,
  input  CLK,
  input  CLR,
  output [15:0] ROW_0,
  output [15:0] ROW_1,
  output [15:0] ROW_2,
  output [15:0] ROW_3
);

  wire demultiplexer_1_out0, demultiplexer_1_out1;

  Demultiplexer #(.enable("false")) demultiplexer_1 (
    .out0(demultiplexer_1_out0), .out1(demultiplexer_1_out1), .in(WRT), .sel(ADDR[1]));
  _2_ROW_GPU u_2_row_gpu_1 (
    .DIN(DIN), .ADDR(ADDR[0]), .WRT(demultiplexer_1_out0), .CLK(CLK), .ROW_0(ROW_0), .ROW_1(ROW_1), .CLR(CLR));
  _2_ROW_GPU u_2_row_gpu_2 (
    .DIN(DIN), .ADDR(ADDR[0]), .WRT(demultiplexer_1_out1), .CLK(CLK), .ROW_0(ROW_2), .ROW_1(ROW_3), .CLR(CLR));
endmodule

module _8_ROW_GPU (
  input  [15:0] DIN,
  input  [2:0] ADDR,
  input  WRT,
  input  CLK,
  input  CLR,
  output [15:0] ROW_0,
  output [15:0] ROW_1,
  output [15:0] ROW_2,
  output [15:0] ROW_3,
  output [15:0] ROW_4,
  output [15:0] ROW_5,
  output [15:0] ROW_6,
  output [15:0] ROW_7
);

  wire demultiplexer_1_out0, demultiplexer_1_out1;

  Demultiplexer #(.enable("false")) demultiplexer_1 (
    .out0(demultiplexer_1_out0), .out1(demultiplexer_1_out1), .in(WRT), .sel(ADDR[2]));
  _4_ROW_GPU u_4_row_gpu_1 (
    .DIN(DIN), .ADDR(ADDR[1:0]), .WRT(demultiplexer_1_out0), .CLK(CLK), .ROW_0(ROW_0), .ROW_1(ROW_1),
    .ROW_2(ROW_2), .ROW_3(ROW_3), .CLR(CLR));
  _4_ROW_GPU u_4_row_gpu_2 (
    .DIN(DIN), .ADDR(ADDR[1:0]), .WRT(demultiplexer_1_out1), .CLK(CLK), .ROW_0(ROW_4), .ROW_1(ROW_5),
    .ROW_2(ROW_6), .ROW_3(ROW_7), .CLR(CLR));
endmodule

module _16_ROW_GPU (
  input  [15:0] DIN,
  input  [3:0] ADDR,
  input  WRT,
  input  CLK,
  input  CLR,
  output [15:0] ROW_0,
  output [15:0] ROW_1,
  output [15:0] ROW_2,
  output [15:0] ROW_3,
  output [15:0] ROW_4,
  output [15:0] ROW_5,
  output [15:0] ROW_6,
  output [15:0] ROW_7,
  output [15:0] ROW_8,
  output [15:0] ROW_9,
  output [15:0] ROW_10,
  output [15:0] ROW_11,
  output [15:0] ROW_12,
  output [15:0] ROW_13,
  output [15:0] ROW_14,
  output [15:0] ROW_15
);

  wire demultiplexer_1_out0, demultiplexer_1_out1;

  Demultiplexer #(.enable("false")) demultiplexer_1 (
    .out0(demultiplexer_1_out0), .out1(demultiplexer_1_out1), .in(WRT), .sel(ADDR[3]));
  _8_ROW_GPU u_8_row_gpu_1 (
    .DIN(DIN), .ADDR(ADDR[2:0]), .WRT(demultiplexer_1_out0), .CLK(CLK), .ROW_0(ROW_0), .ROW_1(ROW_1),
    .ROW_2(ROW_2), .ROW_3(ROW_3), .ROW_4(ROW_4), .ROW_5(ROW_5), .ROW_6(ROW_6), .ROW_7(ROW_7), .CLR(CLR));
  _8_ROW_GPU u_8_row_gpu_2 (
    .DIN(DIN), .ADDR(ADDR[2:0]), .WRT(demultiplexer_1_out1), .CLK(CLK), .ROW_0(ROW_8), .ROW_1(ROW_9),
    .ROW_2(ROW_10), .ROW_3(ROW_11), .ROW_4(ROW_12), .ROW_5(ROW_13), .ROW_6(ROW_14), .ROW_7(ROW_15), .CLR(CLR));
endmodule

module _32_ROW_GPU (
  input  [15:0] DIN,
  input  [4:0] ADDR,
  input  WRT,
  input  CLK,
  input  CLR,
  output [15:0] ROW_0,
  output [15:0] ROW_1,
  output [15:0] ROW_2,
  output [15:0] ROW_3,
  output [15:0] ROW_4,
  output [15:0] ROW_5,
  output [15:0] ROW_6,
  output [15:0] ROW_7,
  output [15:0] ROW_8,
  output [15:0] ROW_9,
  output [15:0] ROW_10,
  output [15:0] ROW_11,
  output [15:0] ROW_12,
  output [15:0] ROW_13,
  output [15:0] ROW_14,
  output [15:0] ROW_15,
  output [15:0] ROW_16,
  output [15:0] ROW_17,
  output [15:0] ROW_18,
  output [15:0] ROW_19,
  output [15:0] ROW_20,
  output [15:0] ROW_21,
  output [15:0] ROW_22,
  output [15:0] ROW_23,
  output [15:0] ROW_24,
  output [15:0] ROW_25,
  output [15:0] ROW_26,
  output [15:0] ROW_27,
  output [15:0] ROW_28,
  output [15:0] ROW_29,
  output [15:0] ROW_30,
  output [15:0] ROW_31
);

  wire demultiplexer_1_out0, demultiplexer_1_out1;

  Demultiplexer #(.enable("false")) demultiplexer_1 (
    .out0(demultiplexer_1_out0), .out1(demultiplexer_1_out1), .in(WRT), .sel(ADDR[4]));
  _16_ROW_GPU u_16_row_gpu_1 (
    .DIN(DIN), .ADDR(ADDR[3:0]), .WRT(demultiplexer_1_out0), .CLK(CLK), .ROW_0(ROW_0), .ROW_1(ROW_1),
    .ROW_2(ROW_2), .ROW_3(ROW_3), .ROW_4(ROW_4), .ROW_5(ROW_5), .ROW_6(ROW_6), .ROW_7(ROW_7), .ROW_8(ROW_8),
    .ROW_9(ROW_9), .ROW_10(ROW_10), .ROW_11(ROW_11), .ROW_12(ROW_12), .ROW_13(ROW_13), .ROW_14(ROW_14),
    .ROW_15(ROW_15), .CLR(CLR));
  _16_ROW_GPU u_16_row_gpu_2 (
    .DIN(DIN), .ADDR(ADDR[3:0]), .WRT(demultiplexer_1_out1), .CLK(CLK), .ROW_0(ROW_16), .ROW_1(ROW_17),
    .ROW_2(ROW_18), .ROW_3(ROW_19), .ROW_4(ROW_20), .ROW_5(ROW_21), .ROW_6(ROW_22), .ROW_7(ROW_23),
    .ROW_8(ROW_24), .ROW_9(ROW_25), .ROW_10(ROW_26), .ROW_11(ROW_27), .ROW_12(ROW_28), .ROW_13(ROW_29),
    .ROW_14(ROW_30), .ROW_15(ROW_31), .CLR(CLR));
endmodule

module _32x32_GPU (
  input  [15:0] DIN,
  input  [5:0] ADDR,
  input  WRT,
  input  CLK,
  input  CLR,
  output [31:0] ROW_0,
  output [31:0] ROW_1,
  output [31:0] ROW_2,
  output [31:0] ROW_3,
  output [31:0] ROW_4,
  output [31:0] ROW_5,
  output [31:0] ROW_6,
  output [31:0] ROW_7,
  output [31:0] ROW_8,
  output [31:0] ROW_9,
  output [31:0] ROW_10,
  output [31:0] ROW_11,
  output [31:0] ROW_12,
  output [31:0] ROW_13,
  output [31:0] ROW_14,
  output [31:0] ROW_15,
  output [31:0] ROW_16,
  output [31:0] ROW_17,
  output [31:0] ROW_18,
  output [31:0] ROW_19,
  output [31:0] ROW_20,
  output [31:0] ROW_21,
  output [31:0] ROW_22,
  output [31:0] ROW_23,
  output [31:0] ROW_24,
  output [31:0] ROW_25,
  output [31:0] ROW_26,
  output [31:0] ROW_27,
  output [31:0] ROW_28,
  output [31:0] ROW_29,
  output [31:0] ROW_30,
  output [31:0] ROW_31
);

  wire demultiplexer_1_out0, demultiplexer_1_out1;

  Demultiplexer #(.enable("false")) demultiplexer_1 (
    .out0(demultiplexer_1_out0), .out1(demultiplexer_1_out1), .in(WRT), .sel(ADDR[5]));
  _32_ROW_GPU u_32_row_gpu_1 (
    .DIN(DIN), .ADDR(ADDR[4:0]), .WRT(demultiplexer_1_out0), .CLK(CLK), .ROW_0(ROW_0[31:16]),
    .ROW_1(ROW_0[15:0]), .ROW_2(ROW_1[31:16]), .ROW_3(ROW_1[15:0]), .ROW_4(ROW_2[31:16]),
    .ROW_5(ROW_2[15:0]), .ROW_6(ROW_3[31:16]), .ROW_7(ROW_3[15:0]), .ROW_8(ROW_4[31:16]),
    .ROW_9(ROW_4[15:0]), .ROW_10(ROW_5[31:16]), .ROW_11(ROW_5[15:0]), .ROW_12(ROW_6[31:16]),
    .ROW_13(ROW_6[15:0]), .ROW_14(ROW_7[31:16]), .ROW_15(ROW_7[15:0]), .ROW_16(ROW_8[31:16]),
    .ROW_17(ROW_8[15:0]), .ROW_18(ROW_9[31:16]), .ROW_19(ROW_9[15:0]), .ROW_20(ROW_10[31:16]),
    .ROW_21(ROW_10[15:0]), .ROW_22(ROW_11[31:16]), .ROW_23(ROW_11[15:0]), .ROW_24(ROW_12[31:16]),
    .ROW_25(ROW_12[15:0]), .ROW_26(ROW_13[31:16]), .ROW_27(ROW_13[15:0]), .ROW_28(ROW_14[31:16]),
    .ROW_29(ROW_14[15:0]), .ROW_30(ROW_15[31:16]), .ROW_31(ROW_15[15:0]), .CLR(CLR));
  _32_ROW_GPU u_32_row_gpu_2 (
    .DIN(DIN), .ADDR(ADDR[4:0]), .WRT(demultiplexer_1_out1), .CLK(CLK), .ROW_0(ROW_16[31:16]),
    .ROW_1(ROW_16[15:0]), .ROW_2(ROW_17[31:16]), .ROW_3(ROW_17[15:0]), .ROW_4(ROW_18[31:16]),
    .ROW_5(ROW_18[15:0]), .ROW_6(ROW_19[31:16]), .ROW_7(ROW_19[15:0]), .ROW_8(ROW_20[31:16]),
    .ROW_9(ROW_20[15:0]), .ROW_10(ROW_21[31:16]), .ROW_11(ROW_21[15:0]), .ROW_12(ROW_22[31:16]),
    .ROW_13(ROW_22[15:0]), .ROW_14(ROW_23[31:16]), .ROW_15(ROW_23[15:0]), .ROW_16(ROW_24[31:16]),
    .ROW_17(ROW_24[15:0]), .ROW_18(ROW_25[31:16]), .ROW_19(ROW_25[15:0]), .ROW_20(ROW_26[31:16]),
    .ROW_21(ROW_26[15:0]), .ROW_22(ROW_27[31:16]), .ROW_23(ROW_27[15:0]), .ROW_24(ROW_28[31:16]),
    .ROW_25(ROW_28[15:0]), .ROW_26(ROW_29[31:16]), .ROW_27(ROW_29[15:0]), .ROW_28(ROW_30[31:16]),
    .ROW_29(ROW_30[15:0]), .ROW_30(ROW_31[31:16]), .ROW_31(ROW_31[15:0]), .CLR(CLR));
endmodule

module KEYBOARD_ADDRESS_DECODER (
  input  [14:0] ADDR,
  output OUT
);

  wire not_1_out, not_2_out, not_3_out, not_4_out, not_5_out, not_6_out, not_7_out;

  not not_1 (not_1_out, ADDR[0]);
  not not_2 (not_2_out, ADDR[1]);
  not not_3 (not_3_out, ADDR[2]);
  not not_4 (not_4_out, ADDR[3]);
  not not_5 (not_5_out, ADDR[4]);
  not not_6 (not_6_out, ADDR[5]);
  not not_7 (not_7_out, ADDR[6]);
  and and_1 (OUT, not_1_out, not_2_out, not_3_out, not_4_out, not_5_out, not_6_out, not_7_out, ADDR[7], ADDR[8], ADDR[9], ADDR[10], ADDR[11], ADDR[12], ADDR[13], ADDR[14]);
endmodule
